// Digital circuit project05.dig as structural Verilog
module project05 (
  input  [1:0] PROG,
  input  CLR,
  input  CLK,
  output DONE,
  output [7:0] ITYPE,
  output [7:0] RTYPE,
  output [7:0] LOAD,
  output [7:0] STYPE,
  output [7:0] BTYPE,
  output [7:0] JAL,
  output [7:0] J,
  output [7:0] JALR,
  output [7:0] TOTAL
);

  wire _8_bit_adder_1_p3, and_1_out, decoder_1_out_0, decoder_1_out_1, decoder_1_out_2, decoder_1_out_3,
       decoder_1_out_4, decoder_1_out_5, decoder_1_out_6, decoder_1_out_7;
  wire [2:0] analyze_decoder_1_p2;
  wire [7:0] _8_bit_adder_1_p2;
  wire [31:0] instruction_memeory_1_d;

  and and_1 (and_1_out, CLK, ~DONE);  // And
  // _8_bit_counter _8_bit_counter_1: pin names not known; wires that end beside it: and_1_out, CLR, TOTAL
  instruction_memeory instruction_memeory_1 (.A(TOTAL), .PN(PROG), .D(instruction_memeory_1_d));
  // _32_bit_eq _32_bit_eq_1: pin names not known; wires that end beside it: instruction_memeory_1_d, 32'hc0001073, DONE
  // analyze_decoder analyze_decoder_1: pin names not known; wires that end beside it: instruction_memeory_1_d, analyze_decoder_1_p2
  // _8_bit_adder _8_bit_adder_1: pin names not known; wires that end beside it: 8'h1, _8_bit_adder_1_p2, _8_bit_adder_1_p3
  Decoder #(.Selector_Bits(3)) decoder_1 (
    .sel(analyze_decoder_1_p2), .out_0(decoder_1_out_0), .out_1(decoder_1_out_1), .out_2(decoder_1_out_2),
    .out_3(decoder_1_out_3), .out_4(decoder_1_out_4), .out_5(decoder_1_out_5), .out_6(decoder_1_out_6),
    .out_7(decoder_1_out_7));
  // _8_bit_register _8_bit_register_1: pin names not known; wires that end beside it: _8_bit_adder_1_p3, and_1_out, decoder_1_out_0, CLR, ITYPE
  // _8_bit_register _8_bit_register_2: pin names not known; wires that end beside it: _8_bit_adder_1_p3, and_1_out, decoder_1_out_1, CLR, RTYPE
  // _8_bit_register _8_bit_register_3: pin names not known; wires that end beside it: _8_bit_adder_1_p3, and_1_out, decoder_1_out_2, CLR, LOAD
  // _8_bit_register _8_bit_register_4: pin names not known; wires that end beside it: _8_bit_adder_1_p3, and_1_out, decoder_1_out_3, CLR, STYPE
  // _8_bit_register _8_bit_register_5: pin names not known; wires that end beside it: _8_bit_adder_1_p3, and_1_out, decoder_1_out_4, CLR, BTYPE
  // _8_bit_register _8_bit_register_6: pin names not known; wires that end beside it: _8_bit_adder_1_p3, and_1_out, decoder_1_out_5, CLR, JAL
  // _8_bit_register _8_bit_register_7: pin names not known; wires that end beside it: _8_bit_adder_1_p3, and_1_out, decoder_1_out_6, CLR, J
  // _8_bit_register _8_bit_register_8: pin names not known; wires that end beside it: _8_bit_adder_1_p3, and_1_out, decoder_1_out_7, CLR, JALR
  Multiplexer #(.Selector_Bits(3), .Bits(8)) multiplexer_1 (
    .sel(analyze_decoder_1_p2), .in_0(ITYPE), .in_1(RTYPE), .in_2(LOAD), .in_3(STYPE), .in_4(BTYPE),
    .in_5(JAL), .in_6(J), .in_7(JALR), .out(_8_bit_adder_1_p2));
endmodule
